# Fritzing sketch MidiMood schematic (saved by Fritzing 0.9.3b)

parts:
  Pro_Micro4 = Pro Micro
  R1 = Rotary Potentiometer (Small) [maximum_resistance=100kΩ package=THT]
  R2 = Rotary Potentiometer (Small) [maximum_resistance=100kΩ package=THT]
  R3 = Rotary Potentiometer (Small) [maximum_resistance=100kΩ package=THT]
  R4 = Rotary Potentiometer (Small) [maximum_resistance=100kΩ package=THT]
  R5 = Rotary Potentiometer (Small) [maximum_resistance=100kΩ package=THT]
  R6 = Rotary Potentiometer (Small) [maximum_resistance=100kΩ package=THT]
  R7 = Rotary Potentiometer (Small) [maximum_resistance=100kΩ package=THT]
  R8 = Rotary Potentiometer (Small) [maximum_resistance=100kΩ package=THT]
  R9 = Rotary Potentiometer (Small) [maximum_resistance=100kΩ package=THT]
  R10 = Rotary Potentiometer (Small) [maximum_resistance=100kΩ package=THT]
  R11 = Rotary Potentiometer (Small) [maximum_resistance=100kΩ package=THT]
  R12 = Rotary Potentiometer (Small) [maximum_resistance=100kΩ package=THT]
  S3 = Toggle Switch spst [package=THT]
  LED1 = smd LED [color="Red (633nm)" package="0805 [SMD]"]
  S4 = Toggle Switch spst [package=THT]
  S5 = Toggle Switch spst [package=THT]
  S6 = Toggle Switch spst [package=THT]
  S7 = Toggle Switch spst [package=THT]
  R13 = Rotary Potentiometer (Small) [maximum_resistance=100kΩ package=THT]
  R14 = Rotary Potentiometer (Small) [maximum_resistance=100kΩ package=THT]
  R15 = Rotary Potentiometer (Small) [maximum_resistance=100kΩ package=THT]
  S8 = Toggle Switch spst [package=THT]
  S9 = Toggle Switch spst [package=THT]
  S10 = Toggle Switch spst [package=THT]
  S11 = Toggle Switch spst [package=THT]
  R16 = Rotary Potentiometer (Small) [maximum_resistance=100kΩ package=THT]
  R18 = Rotary Potentiometer (Small) [maximum_resistance=100kΩ package=THT]
  R19 = Rotary Potentiometer (Small) [maximum_resistance=100kΩ package=THT]
  R20 = Rotary Potentiometer (Small) [maximum_resistance=100kΩ package=THT]
  R21 = Rotary Potentiometer (Small) [maximum_resistance=100kΩ package=THT]
  R22 = Rotary Potentiometer (Small) [maximum_resistance=100kΩ package=THT]
  R23 = Rotary Potentiometer (Small) [maximum_resistance=100kΩ package=THT]
  R24 = Rotary Potentiometer (Small) [maximum_resistance=100kΩ package=THT]
  S12 = Toggle Switch spst [package=THT]
  S13 = Toggle Switch spst [package=THT]
  R25 = Rotary Potentiometer (Small) [maximum_resistance=100kΩ package=THT]
  R26 = Rotary Potentiometer (Small) [maximum_resistance=100kΩ package=THT]
  R27 = Rotary Potentiometer (Small) [maximum_resistance=100kΩ package=THT]
  Part1 = Analog Digital MUX Breakout
  Part2 = Analog Digital MUX Breakout
  R28 = Resistor [tolerance=±5% resistance=220 package="2010 [SMD]"]

nets:
  N1: Pro_Micro4.D2, Part1.S0, Part2.S0
  N2: Pro_Micro4.D3, R28.Pin_1
  N3: Pro_Micro4.D4, Part1.S1, Part2.S1
  N4: Pro_Micro4.D5, Part1.S2, Part2.S2
  N5: Pro_Micro4.D6, Part1.S3, Part2.S3
  N6: Pro_Micro4.D7, S3.L1
  N7: Pro_Micro4.D8, S7.L1
  N8: Pro_Micro4.D9, S6.L1
  N9: Pro_Micro4.D10, S5.L1
  N10: Pro_Micro4.D16/MOSI, S4.L1
  N11: Pro_Micro4.D18/A0, Part2.SIG
  N12: Pro_Micro4.D19/A1, Part1.SIG
  VCC: Pro_Micro4.VCC, R11.leg1, R12.leg1, R13.leg1, R14.leg1, R15.leg1, R16.leg1, R18.leg1, R19.leg1, R20.leg1, R21.leg1, R22.leg1, R23.leg1, R24.leg1, R25.leg1, R26.leg1, R27.leg1, Part1.VCC, Part2.VCC
  GND: Pro_Micro4.GND, R11.leg2, R12.leg2, S4.COM, S5.COM, S6.COM, S7.COM, R13.leg2, R14.leg2, R15.leg2, S8.COM, S9.COM, S10.COM, S11.COM, R16.leg2, R18.leg2, R19.leg2, R20.leg2, R21.leg2, R22.leg2, R23.leg2, R24.leg2, S12.COM, S13.COM, R25.leg2, R26.leg2, R27.leg2, Part1.GND, Part1.EN, Part2.GND, Part2.EN
  N13: R1.leg1, R2.leg1, R3.leg1, R4.leg1, R5.leg1, R6.leg1, R7.leg1, R8.leg1, R9.leg1, R10.leg1
  N14: R1.wiper, Part2.C9
  N15: R1.leg2, R2.leg2, R3.leg2, R4.leg2, R5.leg2, R6.leg2, R7.leg2, R8.leg2, R9.leg2, R10.leg2, S3.COM, LED1.cathode
  N16: R2.wiper, Part2.C6
  N17: R3.wiper, Part2.C3
  N18: R4.wiper, Part2.C0
  N19: R5.wiper, Part2.C1
  N20: R6.wiper, Part2.C4
  N21: R7.wiper, Part2.C7
  N22: R8.wiper, Part2.C8
  N23: R9.wiper, Part2.C5
  N24: R10.wiper, Part2.C2
  N25: R11.wiper, Part1.C14
  N26: R12.wiper, Part1.C15
  N27: R13.wiper, Part1.C11
  N28: R14.wiper, Part1.C13
  N29: R15.wiper, Part1.C12
  N30: S8.L1, Part2.C13
  N31: S9.L1, Part2.C15
  N32: S10.L1, Part2.C14
  N33: S11.L1, Part2.C12
  N34: R16.wiper, Part1.C8
  N35: R18.wiper, Part1.C4
  N36: R19.wiper, Part1.C6
  N37: R20.wiper, Part1.C5
  N38: R21.wiper, Part1.C9
  N39: R22.wiper, Part1.C10
  N40: R23.wiper, Part1.C7
  N41: R24.wiper, Part1.C3
  N42: S12.L1, Part2.C10
  N43: S13.L1, Part2.C11
  N44: R25.wiper, Part1.C0
  N45: R26.wiper, Part1.C2
  N46: R27.wiper, Part1.C1

notes:
  Midi Moog
  by Gustavo Silveira
  A.K.A. Músico Nerd
  gustavosilveira@musiconerd.com
  musiconerd.com
  Arduino Pro Micro
  Multiplexer
  CD4067 (breakout)
  Potentiometer b10k

custom parts:
  Pro Micro: The SparkFun Pro Micro is a complete USB-based microcontoller development system, in a very small footprint, capable of implementing many types of projects. All programming can be done via the USB port.
  Toggle Switch spst: Toggle Switch single pole single throw
